# Fritzing sketch schematic (saved by Fritzing 0.9.1b)
breadboards: 1

parts:
  Parte1 = Arduino Yun
  R2 = Resistor [tolerance=±5% resistance=10k package=THT]
  J1 = Basic Force Sensing Resistor (FSR) [package=THT]
  R4 = Basic Flex Resistor
  R5 = Resistor [tolerance=±5% resistance=330 package=THT]
  3-Axis_Accelerometer1 = 3-Axis Accelerometer Breakout - MMA8452Q
  R6 = Resistor [tolerance=±5% resistance=330 package=THT]
  R7 = Resistor [tolerance=±5% resistance=10k package=THT]

nets:
  N1: Parte1.A0, R2.Pin_1, R4.pin_1
  N2: Parte1.A1, J1.pin_0, R7.Pin_1
  GND: Parte1.GND, J1.pin_1, R4.Pin_2, 3-Axis_Accelerometer1.GND
  N3: Parte1.A4/SDA, R6.Pin_0
  N4: Parte1.A5/SCL, R5.Pin_0
  3V3: Parte1.3V3, 3-Axis_Accelerometer1.3.3V
  N5: Parte1.5V, R2.Pin_0, R7.Pin_0
  N6: R5.Pin_1, 3-Axis_Accelerometer1.SCL, 3-Axis_Accelerometer1.I2
  N7: 3-Axis_Accelerometer1.SDA, R6.Pin_1
